// Logisim project LabArqui.circ as structural Verilog
module OneBitComparer (
  input  A,
  input  B,
  output AGB,
  output AEB,
  output ALB
);

  wire not_1_out, not_2_out, or_1_out;

  not not_1 (not_1_out, B);
  not not_2 (not_2_out, A);
  and and_1 (AGB, A, not_1_out);
  buf and_2 (ALB, not_2_out);  // AND_Gate
  or or_1 (or_1_out, AGB, ALB);
  not not_3 (AEB, or_1_out);

  // Notes on the sheet:
  //   A>B
  //   A=B
  //   A<B
endmodule

module EightBitComparer (
  input  in_1,
  input  in_2
);

  OneBitComparer onebitcomparer_1 ();  // open: A, B, AGB, AEB, ALB
endmodule
